// Digital circuit ALU.dig as structural Verilog
module ALU (
  input  [7:0] A,
  input  [7:0] TMP,
  input  El,
  input  [3:0] Sel,
  output [7:0] Q,
  output [7:0] Flag
);

  wire [7:0] ADD, AND, CMA, DCR, INC, multiplexer_1_out, multiplexer_2_out, OR, RAL, RAR, SUB, XOR;

  assign Q = El ? multiplexer_1_out : 8'bz;  // Driver driver_1
  Multiplexer #(.Bits(8)) multiplexer_1 (.sel(Sel[3]), .in_0(Flag), .in_1(multiplexer_2_out), .out(multiplexer_1_out));
  Multiplexer #(.Selector_Bits(3), .Bits(8)) multiplexer_2 (
    .sel(Sel[2:0]), .in_0(CMA), .in_1(RAL), .in_2(RAR), .in_3({8{1'b0}}), .in_4({8{1'b0}}), .in_5({8{1'b0}}),
    .in_6({8{1'b0}}), .in_7({8{1'b0}}), .out(multiplexer_2_out));
  Multiplexer #(.Selector_Bits(3), .Bits(8)) multiplexer_3 (
    .sel(Sel[2:0]), .in_0(ADD), .in_1(SUB), .in_2(INC), .in_3(DCR), .in_4(AND), .in_5(OR), .in_6(XOR),
    .in_7({8{1'b0}}), .out(Flag));
  assign CMA = ~A;  // Not not_1, 8 bits wide
  assign AND = TMP & A;  // And and_1, 8 bits wide
  Add #(.Bits(8)) u_INC (.a(TMP), .b(8'h1), .c_i(1'b0), .s(INC));  // open: c_o
  Add #(.Bits(8)) u_ADD (.a(A), .b(TMP), .c_i(1'b0), .s(ADD));  // open: c_o
  BarrelShifter #(.Bits(8), .barrelShifterMode("rotate")) u_RAL (.in(A), .shift(4'b0001), .out(RAL));
  assign OR = TMP | A;  // Or or_1, 8 bits wide
  Sub #(.Bits(8)) u_DCR (.a(TMP), .b(8'h1), .c_i(1'b0), .s(DCR));  // open: c_o
  Sub #(.Bits(8)) u_SUB (.a(A), .b(TMP), .c_i(1'b0), .s(SUB));  // open: c_o
  BarrelShifter #(.Bits(8), .barrelShifterMode("rotate"), .direction("right")) u_RAR (
    .in(A), .shift(4'b0001), .out(RAR));
  assign XOR = TMP ^ A;  // XOr xor_1, 8 bits wide

  // Notes on the sheet:
  //   A: Sel:
  //   0: Add
  //   1: Sub
  //   2: Increment
  //   3: Decrement
  //   4: AND
  //   5: OR
  //   6: XOR
  //   7: CMA
  //   8: RAL
  //   9: RAR
  //   Sel: Sel:
  //   0: Add
  //   1: Sub
  //   2: Increment
  //   3: Decrement
  //   4: AND
  //   5: OR
  //   6: XOR
  //   7: CMA
  //   8: RAL
  //   9: RAR
  //   Sel:
  //   0: Add
  //   1: Sub
  //   2: Increment
  //   3: Decrement
  //   4: AND
  //   5: OR
  //   6: XOR
  //   8: CMA
  //   9: RAL
  //   10: RAR
endmodule
