// Digital circuit Accumulator.dig as structural Verilog
module Accumulator (
  input  [7:0] A,
  input  nLa,
  input  CLK,
  input  Ea,
  output [7:0] D,
  output [7:0] ASout
);

  assign D = Ea ? ASout : 8'bz;  // Driver driver_1
  D8_wEnableAsyncClear d8_wenableasyncclear_1 (
    .D0(A[0]), .D1(A[1]), .D2(A[2]), .D3(A[3]), .D4(A[4]), .D5(A[5]), .D6(A[6]), .D7(A[7]), .nE(nLa),
    .CLK(CLK), .CLR(1'b0), .Q0(ASout[0]), .Q1(ASout[1]), .Q2(ASout[2]), .Q3(ASout[3]), .Q4(ASout[4]),
    .Q5(ASout[5]), .Q6(ASout[6]), .Q7(ASout[7]));

  // Notes on the sheet:
  //   A: Input coming from the bus
  //   D: Output going to the bus
endmodule
