// Digital circuit B register.dig as structural Verilog
module B_register (
  input  nLb,
  input  CLK,
  input  [7:0] B,
  input  Eb,
  output [7:0] Q
);

  wire [7:0] d8_wenableasyncclear_1_q7;

  assign Q = Eb ? d8_wenableasyncclear_1_q7 : 8'bz;  // Driver driver_1
  D8_wEnableAsyncClear d8_wenableasyncclear_1 (
    .D0(B[0]), .D1(B[1]), .D2(B[2]), .D3(B[3]), .D4(B[4]), .D5(B[5]), .D6(B[6]), .D7(B[7]), .nE(nLb),
    .CLK(CLK), .CLR(1'b0), .Q0(d8_wenableasyncclear_1_q7[0]), .Q1(d8_wenableasyncclear_1_q7[1]),
    .Q2(d8_wenableasyncclear_1_q7[2]), .Q3(d8_wenableasyncclear_1_q7[3]), .Q4(d8_wenableasyncclear_1_q7[4]),
    .Q5(d8_wenableasyncclear_1_q7[5]), .Q6(d8_wenableasyncclear_1_q7[6]), .Q7(d8_wenableasyncclear_1_q7[7]));

  // Notes on the sheet:
  //   B: Input coming from the bus
  //   Q: Output going to adder-subtractor
endmodule
