// Digital circuit C register.dig as structural Verilog
module C_register (
  input  nLc,
  input  CLK,
  input  [7:0] C,
  input  Ec,
  output [7:0] Q
);

  wire [7:0] d8_wenableasyncclear_1_q7;

  assign Q = Ec ? d8_wenableasyncclear_1_q7 : 8'bz;  // Driver driver_1
  D8_wEnableAsyncClear d8_wenableasyncclear_1 (
    .D0(C[0]), .D1(C[1]), .D2(C[2]), .D3(C[3]), .D4(C[4]), .D5(C[5]), .D6(C[6]), .D7(C[7]), .nE(nLc),
    .CLK(CLK), .CLR(1'b0), .Q0(d8_wenableasyncclear_1_q7[0]), .Q1(d8_wenableasyncclear_1_q7[1]),
    .Q2(d8_wenableasyncclear_1_q7[2]), .Q3(d8_wenableasyncclear_1_q7[3]), .Q4(d8_wenableasyncclear_1_q7[4]),
    .Q5(d8_wenableasyncclear_1_q7[5]), .Q6(d8_wenableasyncclear_1_q7[6]), .Q7(d8_wenableasyncclear_1_q7[7]));

  // Notes on the sheet:
  //   C: Input coming from the bus
  //   Q: Output going to adder-subtractor
endmodule
