// Digital circuit ClockGen.dig as structural Verilog
module ClockGen (
  input  nA_M,
  input  St,
  input  HLT,
  input  RESET,
  input  Cin,
  input  nReady,
  output nCLR,
  output CLR,
  output nCLK,
  output CLK
);

  wire and_1_out, multiplexer_1_out;

  Multiplexer multiplexer_1 (.sel(nA_M), .in_0(Cin), .in_1(St), .out(multiplexer_1_out));
  RS_FF_AS rs_ff_as_1 (.S(Cin), .R(RESET), .nQ(CLR));  // open: Q
  and and_1 (and_1_out, multiplexer_1_out, ~HLT);  // And
  not not_1 (nCLR, CLR);
  and and_2 (CLK, ~nReady, and_1_out);  // And
  not not_2 (nCLK, CLK);

  // Notes on the sheet:
  //   nA_M: A: 0
  //   Cin: Hz: 200
endmodule
