// Digital circuit Counter8wAsyncClear.dig as structural Verilog
module Counter8wAsyncClear (
  input  nLD,
  input  nCLR,
  input  CLK,
  input  ENT,
  input  ENP,
  input  [7:0] D,
  output RCO,
  output [7:0] Q
);

  wire and_1_out, comparator_1_eq;
  wire [7:0] add_1_s, multiplexer_1_out, multiplexer_2_out, multiplexer_3_out;

  Add #(.Bits(8)) add_1 (.a(Q), .b(8'h1), .c_i(1'b0), .s(add_1_s));  // open: c_o
  and and_1 (and_1_out, ENP, ENT);
  Comparator #(.Bits(8)) comparator_1 (.a(Q), .b({8{1'b1}}), .eq(comparator_1_eq));  // open: gt, lt
  Multiplexer #(.Bits(8)) multiplexer_1 (
    .sel(comparator_1_eq), .in_0(add_1_s), .in_1({8{1'b0}}), .out(multiplexer_1_out));
  Multiplexer #(.Bits(8)) multiplexer_2 (.sel(and_1_out), .in_0(Q), .in_1(multiplexer_1_out), .out(multiplexer_2_out));
  Multiplexer #(.Bits(8)) multiplexer_3 (.sel(nLD), .in_0(D), .in_1(multiplexer_2_out), .out(multiplexer_3_out));
  D_FF_AS #(.Bits(8)) d_ff_as_1 (.Set(1'b0), .D(multiplexer_3_out), .C(CLK), .Clr(~nCLR), .Q(Q));  // open: nQ
  and and_2 (RCO, comparator_1_eq, ENT);

  // Notes on the sheet:
  //   nLD: pin 9
  //   nCLR: pin 1
  //   CLK: pin 2, Hz: 5
  //   RCO: pin 15
  //   ENT: pin 10
  //   ENP: pin 7
  //   D: pin 1
endmodule
