// Digital circuit D4-wEnableAsyncClear.dig as structural Verilog
module D4_wEnableAsyncClear (
  input  D0,
  input  nE,
  input  CLK,
  input  CLR,
  input  D1,
  input  D2,
  input  D3,
  output Q0,
  output Q1,
  output Q2,
  output Q3
);

  wire and_1_out, and_2_out, and_3_out, and_4_out, and_5_out, and_6_out, and_7_out, and_8_out, not_1_out,
       or_1_out, or_2_out, or_3_out, or_4_out;

  not not_1 (not_1_out, nE);
  and and_1 (and_1_out, Q0, nE);
  and and_2 (and_2_out, D0, not_1_out);
  and and_3 (and_3_out, Q1, nE);
  and and_4 (and_4_out, D1, not_1_out);
  and and_5 (and_5_out, Q2, nE);
  and and_6 (and_6_out, D2, not_1_out);
  and and_7 (and_7_out, Q3, nE);
  and and_8 (and_8_out, D3, not_1_out);
  or or_1 (or_1_out, and_1_out, and_2_out);
  or or_2 (or_2_out, and_3_out, and_4_out);
  or or_3 (or_3_out, and_5_out, and_6_out);
  or or_4 (or_4_out, and_7_out, and_8_out);
  D_FF_AS d_ff_as_1 (.Set(1'b0), .D(or_1_out), .C(CLK), .Clr(CLR), .Q(Q0));  // open: nQ
  D_FF_AS d_ff_as_2 (.Set(1'b0), .D(or_2_out), .C(CLK), .Clr(CLR), .Q(Q1));  // open: nQ
  D_FF_AS d_ff_as_3 (.Set(1'b0), .D(or_3_out), .C(CLK), .Clr(CLR), .Q(Q2));  // open: nQ
  D_FF_AS d_ff_as_4 (.Set(1'b0), .D(or_4_out), .C(CLK), .Clr(CLR), .Q(Q3));  // open: nQ

  // Notes on the sheet:
  //   nE: default 1
  //   CLR: default 1
endmodule
