// Digital circuit D8-Latch.dig as structural Verilog
module D8_Latch (
  input  D0,
  input  D1,
  input  D2,
  input  D3,
  input  D4,
  input  D5,
  input  D6,
  input  D7,
  input  E,
  output Q0,
  output Q1,
  output Q2,
  output Q3,
  output Q4,
  output Q5,
  output Q6,
  output Q7
);

  // D_Latch d_latch_1: pin names not known; wires that end beside it: D0, E, Q0
  // D_Latch d_latch_2: pin names not known; wires that end beside it: D1, E, Q1
  // D_Latch d_latch_3: pin names not known; wires that end beside it: D2, E, Q2
  // D_Latch d_latch_4: pin names not known; wires that end beside it: D3, E, Q3
  // D_Latch d_latch_5: pin names not known; wires that end beside it: D4, E, Q4
  // D_Latch d_latch_6: pin names not known; wires that end beside it: D5, E, Q5
  // D_Latch d_latch_7: pin names not known; wires that end beside it: D6, E, Q6
  // D_Latch d_latch_8: pin names not known; wires that end beside it: D7, E, Q7

  // Notes on the sheet:
  //   E: Input Enable
endmodule
