// Digital circuit D8-wEnableAsyncClear.dig as structural Verilog
module D8_wEnableAsyncClear (
  input  D0,
  input  nE,
  input  CLK,
  input  CLR,
  input  D1,
  input  D2,
  input  D3,
  input  D4,
  input  D5,
  input  D6,
  input  D7,
  output Q0,
  output Q1,
  output Q2,
  output Q3,
  output Q4,
  output Q5,
  output Q6,
  output Q7
);

  wire and_1_out, and_2_out, and_3_out, and_4_out, and_5_out, and_6_out, and_7_out, and_8_out, and_9_out,
       and_10_out, and_11_out, and_12_out, and_13_out, and_14_out, and_15_out, and_16_out, not_1_out,
       or_1_out, or_2_out, or_3_out, or_4_out, or_5_out, or_6_out, or_7_out, or_8_out;

  not not_1 (not_1_out, nE);
  and and_1 (and_1_out, Q0, nE);
  and and_2 (and_2_out, D0, not_1_out);
  and and_3 (and_3_out, Q1, nE);
  and and_4 (and_4_out, D1, not_1_out);
  and and_5 (and_5_out, Q2, nE);
  and and_6 (and_6_out, D2, not_1_out);
  and and_7 (and_7_out, Q3, nE);
  and and_8 (and_8_out, D3, not_1_out);
  and and_9 (and_9_out, Q4, nE);
  and and_10 (and_10_out, D4, not_1_out);
  and and_11 (and_11_out, Q5, nE);
  and and_12 (and_12_out, D5, not_1_out);
  and and_13 (and_13_out, Q6, nE);
  and and_14 (and_14_out, D6, not_1_out);
  and and_15 (and_15_out, Q7, nE);
  and and_16 (and_16_out, D7, not_1_out);
  or or_1 (or_1_out, and_1_out, and_2_out);
  or or_2 (or_2_out, and_3_out, and_4_out);
  or or_3 (or_3_out, and_5_out, and_6_out);
  or or_4 (or_4_out, and_7_out, and_8_out);
  or or_5 (or_5_out, and_9_out, and_10_out);
  or or_6 (or_6_out, and_11_out, and_12_out);
  or or_7 (or_7_out, and_13_out, and_14_out);
  or or_8 (or_8_out, and_15_out, and_16_out);
  D_FF_AS d_ff_as_1 (.Set(1'b0), .D(or_1_out), .C(CLK), .Clr(CLR), .Q(Q0));  // open: nQ
  D_FF_AS d_ff_as_2 (.Set(1'b0), .D(or_2_out), .C(CLK), .Clr(CLR), .Q(Q1));  // open: nQ
  D_FF_AS d_ff_as_3 (.Set(1'b0), .D(or_3_out), .C(CLK), .Clr(CLR), .Q(Q2));  // open: nQ
  D_FF_AS d_ff_as_4 (.Set(1'b0), .D(or_4_out), .C(CLK), .Clr(CLR), .Q(Q3));  // open: nQ
  D_FF_AS d_ff_as_5 (.Set(1'b0), .D(or_5_out), .C(CLK), .Clr(CLR), .Q(Q4));  // open: nQ
  D_FF_AS d_ff_as_6 (.Set(1'b0), .D(or_6_out), .C(CLK), .Clr(CLR), .Q(Q5));  // open: nQ
  D_FF_AS d_ff_as_7 (.Set(1'b0), .D(or_7_out), .C(CLK), .Clr(CLR), .Q(Q6));  // open: nQ
  D_FF_AS d_ff_as_8 (.Set(1'b0), .D(or_8_out), .C(CLK), .Clr(CLR), .Q(Q7));  // open: nQ

  // Notes on the sheet:
  //   nE: default 1
  //   CLR: default 1
endmodule
