// Digital circuit D8M-Latch.dig as structural Verilog
module D8M_Latch (
  input  E,
  input  [7:0] D,
  output [7:0] Q
);

  // D_Latch d_latch_1: pin names not known; wires that end beside it: D[0], E, Q[0]
  // D_Latch d_latch_2: pin names not known; wires that end beside it: D[1], E, Q[1]
  // D_Latch d_latch_3: pin names not known; wires that end beside it: D[2], E, Q[2]
  // D_Latch d_latch_4: pin names not known; wires that end beside it: D[3], E, Q[3]
  // D_Latch d_latch_5: pin names not known; wires that end beside it: D[4], E, Q[4]
  // D_Latch d_latch_6: pin names not known; wires that end beside it: D[5], E, Q[5]
  // D_Latch d_latch_7: pin names not known; wires that end beside it: D[6], E, Q[6]
  // D_Latch d_latch_8: pin names not known; wires that end beside it: D[7], E, Q[7]

  // Notes on the sheet:
  //   E: Input Enable
  //   D: Input Enable
endmodule
