// Digital circuit Flags.dig as structural Verilog
module Flags (
  input  [7:0] F,
  input  CLK,
  input  CLR,
  input  Eflag,
  output Sign,
  output Zero
);

  wire not_1_out;
  wire [6:0] d8_wenableasyncclear_1_q3;

  not not_1 (not_1_out, Eflag);
  D8_wEnableAsyncClear d8_wenableasyncclear_1 (
    .D0(F[0]), .D1(F[1]), .D2(F[2]), .D3(F[3]), .D4(F[4]), .D5(F[5]), .D6(F[6]), .D7(F[7]), .nE(not_1_out),
    .CLK(CLK), .CLR(CLR), .Q0(d8_wenableasyncclear_1_q3[0]), .Q1(d8_wenableasyncclear_1_q3[1]),
    .Q2(d8_wenableasyncclear_1_q3[2]), .Q3(d8_wenableasyncclear_1_q3[3]), .Q4(d8_wenableasyncclear_1_q3[4]),
    .Q5(d8_wenableasyncclear_1_q3[5]), .Q6(d8_wenableasyncclear_1_q3[6]), .Q7(Sign));
  // Probe on {Sign, d8_wenableasyncclear_1_q3}
  Comparator #(.Bits(8)) comparator_1 (
    .a({Sign, d8_wenableasyncclear_1_q3}), .b({8{1'b0}}), .eq(Zero));  // open: gt, lt
endmodule
