// Digital circuit IOCon.dig as structural Verilog
module IOCon (
  input  IOEn,
  input  nCLK,
  input  CLR,
  input  nLio,
  input  [7:0] IOSel,
  output Ei1,
  output Ei2,
  output nLo3,
  output nLo4,
  output [7:0] IOp
);

  wire demultiplexer_1_out_3, demultiplexer_1_out_4;

  D8_wEnableAsyncClear d8_wenableasyncclear_1 (
    .D0(IOSel[0]), .D1(IOSel[1]), .D2(IOSel[2]), .D3(IOSel[3]), .D4(IOSel[4]), .D5(IOSel[5]), .D6(IOSel[6]),
    .D7(IOSel[7]), .nE(nLio), .CLK(nCLK), .CLR(CLR), .Q0(IOp[0]), .Q1(IOp[1]), .Q2(IOp[2]), .Q3(IOp[3]),
    .Q4(IOp[4]), .Q5(IOp[5]), .Q6(IOp[6]), .Q7(IOp[7]));
  Demultiplexer #(.Selector_Bits(3)) demultiplexer_1 (
    .sel(IOp[2:0]), .in(IOEn), .out_1(Ei1), .out_2(Ei2), .out_3(demultiplexer_1_out_3),
    .out_4(demultiplexer_1_out_4));  // open: out_0, out_5, out_6, out_7
  not not_1 (nLo3, demultiplexer_1_out_3);
  not not_2 (nLo4, demultiplexer_1_out_4);
endmodule
