// Digital circuit IR.dig as structural Verilog
module IR (
  input  [7:0] B,
  input  nLi,
  input  CLK,
  input  CLR,
  output [7:0] C
);

  D8_wEnableAsyncClear d8_wenableasyncclear_1 (
    .D0(B[0]), .D1(B[1]), .D2(B[2]), .D3(B[3]), .D4(B[4]), .D5(B[5]), .D6(B[6]), .D7(B[7]), .nE(nLi),
    .CLK(CLK), .CLR(CLR), .Q0(C[0]), .Q1(C[1]), .Q2(C[2]), .Q3(C[3]), .Q4(C[4]), .Q5(C[5]), .Q6(C[6]),
    .Q7(C[7]));

  // Notes on the sheet:
  //   B: Input coming from bus
  //   C: Output going to the controller
endmodule
