// Digital circuit Input port 1.dig as structural Verilog
module Input_port_1 (
  input  Ein1,
  input  CLK,
  input  [7:0] Kb,
  output [7:0] Q
);

  wire [7:0] d8_wenableasyncclear_1_q0;

  D8_wEnableAsyncClear d8_wenableasyncclear_1 (
    .D0(Kb[0]), .D1(Kb[1]), .D2(Kb[2]), .D3(Kb[3]), .D4(Kb[4]), .D5(Kb[5]), .D6(Kb[6]), .D7(Kb[7]),
    .nE(1'b0), .CLK(CLK), .CLR(1'b0), .Q0(d8_wenableasyncclear_1_q0[0]), .Q1(d8_wenableasyncclear_1_q0[1]),
    .Q2(d8_wenableasyncclear_1_q0[2]), .Q3(d8_wenableasyncclear_1_q0[3]), .Q4(d8_wenableasyncclear_1_q0[4]),
    .Q5(d8_wenableasyncclear_1_q0[5]), .Q6(d8_wenableasyncclear_1_q0[6]), .Q7(d8_wenableasyncclear_1_q0[7]));
  assign Q = Ein1 ? d8_wenableasyncclear_1_q0 : 8'bz;  // Driver driver_1
endmodule
