// Digital circuit Input port 2.dig as structural Verilog
module Input_port_2 (
  input  CLK,
  input  R,
  input  Si,
  input  SinEx,
  input  Ein2,
  output [7:0] Q
);

  wire [7:0] d8_wenableasyncclear_1_q0;

  D8_wEnableAsyncClear d8_wenableasyncclear_1 (
    .D0(R), .D1(1'b0), .D2(1'b0), .D3(1'b0), .D4(1'b0), .D5(1'b0), .D6(SinEx), .D7(Si), .nE(1'b0), .CLK(CLK),
    .CLR(1'b0), .Q0(d8_wenableasyncclear_1_q0[0]), .Q1(d8_wenableasyncclear_1_q0[1]),
    .Q2(d8_wenableasyncclear_1_q0[2]), .Q3(d8_wenableasyncclear_1_q0[3]), .Q4(d8_wenableasyncclear_1_q0[4]),
    .Q5(d8_wenableasyncclear_1_q0[5]), .Q6(d8_wenableasyncclear_1_q0[6]), .Q7(d8_wenableasyncclear_1_q0[7]));
  assign Q = Ein2 ? d8_wenableasyncclear_1_q0 : 8'bz;  // Driver driver_1
endmodule
