// Digital circuit MAR.dig as structural Verilog
module MAR (
  input  nLm,
  input  CLK,
  input  CLR,
  input  [2:0] Msel,
  input  [15:0] A,
  output [15:0] Q
);

  wire [15:0] multiplexer_1_out;

  D16_wEnableAsyncClear d16_wenableasyncclear_1 (
    .D0(multiplexer_1_out[0]), .D1(multiplexer_1_out[1]), .D2(multiplexer_1_out[2]),
    .D3(multiplexer_1_out[3]), .D4(multiplexer_1_out[4]), .D5(multiplexer_1_out[5]),
    .D6(multiplexer_1_out[6]), .D7(multiplexer_1_out[7]), .D8(multiplexer_1_out[8]),
    .D9(multiplexer_1_out[9]), .D10(multiplexer_1_out[10]), .D11(multiplexer_1_out[11]),
    .D12(multiplexer_1_out[12]), .D13(multiplexer_1_out[13]), .D14(multiplexer_1_out[14]),
    .D15(multiplexer_1_out[15]), .nE(nLm), .CLK(CLK), .CLR(CLR), .Q0(Q[0]), .Q1(Q[1]), .Q2(Q[2]), .Q3(Q[3]),
    .Q4(Q[4]), .Q5(Q[5]), .Q6(Q[6]), .Q7(Q[7]), .Q8(Q[8]), .Q9(Q[9]), .Q10(Q[10]), .Q11(Q[11]), .Q12(Q[12]),
    .Q13(Q[13]), .Q14(Q[14]), .Q15(Q[15]));
  Multiplexer #(.Selector_Bits(3), .Bits(16)) multiplexer_1 (
    .sel(Msel), .in_0(A), .in_1(16'hfffe), .in_2({16{1'b1}}), .in_3(16'hfffb), .in_4(16'hfffc),
    .in_5({16{1'b0}}), .in_6({16{1'b0}}), .in_7({16{1'b0}}), .out(multiplexer_1_out));

  // Notes on the sheet:
  //   Q: Output going to the RAM
  //   Msel: 0: Input from PC
  //   1: FFFE
  //   2: FFFF
  //   3: FFFB
  //   4: FFFC
  //   A: Input coming from the bus
endmodule
