// Digital circuit MDR.dig as structural Verilog
module MDR (
  input  [7:0] DBs,
  input  nLmdr,
  input  CLK,
  input  Emdr,
  input  DIR,
  input  [7:0] IRAM,
  output [7:0] ORAM,
  output [7:0] OBs
);

  wire [7:0] TO_BUS_q0, TO_RAM_q7;

  assign ORAM = DIR ? TO_RAM_q7 : 8'bz;  // Driver driver_1
  D8_wEnableAsyncClear TO_BUS (
    .D0(IRAM[0]), .D1(IRAM[1]), .D2(IRAM[2]), .D3(IRAM[3]), .D4(IRAM[4]), .D5(IRAM[5]), .D6(IRAM[6]),
    .D7(IRAM[7]), .nE(DIR), .CLK(CLK), .CLR(1'b0), .Q0(TO_BUS_q0[0]), .Q1(TO_BUS_q0[1]), .Q2(TO_BUS_q0[2]),
    .Q3(TO_BUS_q0[3]), .Q4(TO_BUS_q0[4]), .Q5(TO_BUS_q0[5]), .Q6(TO_BUS_q0[6]), .Q7(TO_BUS_q0[7]));
  D8_wEnableAsyncClear TO_RAM (
    .D0(DBs[0]), .D1(DBs[1]), .D2(DBs[2]), .D3(DBs[3]), .D4(DBs[4]), .D5(DBs[5]), .D6(DBs[6]), .D7(DBs[7]),
    .nE(nLmdr), .CLK(CLK), .CLR(1'b0), .Q0(TO_RAM_q7[0]), .Q1(TO_RAM_q7[1]), .Q2(TO_RAM_q7[2]),
    .Q3(TO_RAM_q7[3]), .Q4(TO_RAM_q7[4]), .Q5(TO_RAM_q7[5]), .Q6(TO_RAM_q7[6]), .Q7(TO_RAM_q7[7]));
  assign OBs = Emdr ? TO_BUS_q0 : 8'bz;  // Driver driver_2

  // Notes on the sheet:
  //   ORAM: Output going to the RAM
  //   Emdr: Enabler for bus transfer
  //   DIR: 0: RAM to BUS
  //   1: BUS to RAM
endmodule
