// Digital circuit Output Port 4.dig as structural Verilog
module Output_Port_4 (
  input  [7:0] DBs,
  input  nLo4,
  input  CLK,
  input  CLR,
  output [7:0] Q,
  output So,
  output ACK
);

  D8_wEnableAsyncClear d8_wenableasyncclear_1 (
    .D0(DBs[0]), .D1(DBs[1]), .D2(DBs[2]), .D3(DBs[3]), .D4(DBs[4]), .D5(DBs[5]), .D6(DBs[6]), .D7(DBs[7]),
    .nE(nLo4), .CLK(CLK), .CLR(CLR), .Q0(Q[0]), .Q1(Q[1]), .Q2(Q[2]), .Q3(Q[3]), .Q4(Q[4]), .Q5(Q[5]),
    .Q6(Q[6]), .Q7(ACK));

  assign Q[7] = ACK;
  assign So = Q[0];
endmodule
