// Digital circuit PC.dig as structural Verilog
module PC (
  input  Cp,
  input  Ep,
  input  Ld,
  input  nCLR,
  input  nCLK,
  input  As,
  input  [7:0] Alb,
  input  [7:0] Ahb,
  input  LAIn,
  input  PCSel,
  output [15:0] DP,
  output [15:0] Ain,
  output [7:0] Q,
  output [15:0] D
);

  wire demultiplexer_1_out_0, demultiplexer_1_out_1;
  wire [7:0] multiplexer_1_out;

  Demultiplexer demultiplexer_1 (.sel(As), .in(LAIn), .out_0(demultiplexer_1_out_0), .out_1(demultiplexer_1_out_1));
  D8M_Latch d8m_latch_1 (.E(demultiplexer_1_out_0), .D(Alb), .Q(Ain[7:0]));
  D8M_Latch d8m_latch_2 (.E(demultiplexer_1_out_1), .D(Ahb), .Q(Ain[15:8]));
  CounterPreset #(.Bits(16)) counterpreset_1 (
    .en(Cp), .C(nCLK), .dir(1'b0), .in(Ain), .ld(Ld), .clr(~nCLR), .out(DP));  // open: ovf
  assign D = Ep ? DP : 16'bz;  // Driver driver_1
  Multiplexer #(.Bits(8)) multiplexer_1 (.sel(PCSel), .in_0(DP[7:0]), .in_1(DP[15:8]), .out(multiplexer_1_out));
  assign Q = Ep ? multiplexer_1_out : 8'bz;  // Driver driver_2

  // Notes on the sheet:
  //   DP: Output going to the bus
  //   Q: Output going to the bus
  //   D: Output going to the bus
endmodule
