// Digital circuit RAM AND ROM.dig as structural Verilog
module RAM_AND_ROM (
  input  [15:0] IMAR,
  input  [7:0] IMDR,
  input  nCLK,
  input  [15:0] SA,
  input  [15:0] EA,
  input  nRun_Prog,
  input  DIR,
  input  Write,
  output [7:0] OMDR,
  output nEoa
);

  wire E, multiplexer_2_out, not_1_out;
  wire [7:0] ramsingleportsel_1_d, ROMVALUE;
  wire [15:0] A_ROM, multiplexer_3_out;

  RRCounter rrcounter_1 (.EA(EA), .CLK(nCLK), .SA(SA), .Write(Write), .nEoa(nEoa), .A_ROM(A_ROM));
  ROM #(.AddrBits(16), .Bits(8)) rom_1 (.A(A_ROM), .sel(1'b1), .D(ROMVALUE));
  // Probe on ROMVALUE
  not not_1 (not_1_out, DIR);
  Multiplexer multiplexer_1 (.sel(nRun_Prog), .in_0(DIR), .in_1(1'b0), .out(E));
  Multiplexer multiplexer_2 (.sel(nRun_Prog), .in_0(not_1_out), .in_1(1'b0), .out(multiplexer_2_out));
  Multiplexer #(.Bits(16)) multiplexer_3 (.sel(nRun_Prog), .in_0(IMAR), .in_1(A_ROM), .out(multiplexer_3_out));
  RAMSinglePortSel #(.AddrBits(16), .Bits(8)) ramsingleportsel_1 (
    .A(multiplexer_3_out), .CS(1'b1), .WE(~multiplexer_2_out), .OE(multiplexer_2_out),
    .D(ramsingleportsel_1_d));
  assign ramsingleportsel_1_d = nRun_Prog ? ROMVALUE : 8'bz;  // Driver driver_1
  assign ramsingleportsel_1_d = E ? IMDR : 8'bz;  // Driver driver_2
  assign OMDR = ~E ? ramsingleportsel_1_d : 8'bz;  // DriverInvSel driverinvsel_1
  // Probe on ramsingleportsel_1_d

  // Other names for the same wires on the sheet: Mode = nRun_Prog

  // Notes on the sheet:
  //   OMDR: Output going to MDR
  //   IMAR: Input from MAR
  //   IMDR: Input from MDR
  //   nCLK: Next Address.
  //   For Starting input to be recorded, press N button
  //   SA: Starting Address
  //   EA: Ending Address
  //   nRun_Prog: 0: Run Mode (Enable)
  //   1; Prorgamming Mode
  //   DIR: 0: Prorgamming Mode
  //   1: Run Mode (Enable)
  //   Write: 0: Prorgamming Mode
  //   1: Run Mode (Enable)
  //   Note:
  //   1. Press N then We after setting the starding address
  //   contents of rom_1 (hex, n*v repeats v):
  //   3e,33,3c,3c,c3,0,0,76,0,0,0,0,0,0,0,0,0,0,0,0,0,0,0,0,0,0,0,0,0,0,0,0,0,0,0,0,0,0,
  //   0,0,0,0,0,0,0,0,0,0,0,0,0,0,0,0,0,0,0,0,0,0,0,0,0,0,0,0,0,0,0,0,0,0,0,0,0,0,0,0,0,
  //   0,0,0,0,0,0,0,0,0,0,0,0,0,0,0,0,0,0,0,0,0,0,0,0,0,0,0,0,0,0,0,0,0,0,0,0,0,0,0,0,0,
  //   0,0,0,0,0,0,0,0,0,0,0,0,0,0,0,0,0,0,0,0,0,0,0,0,0,0,0,0,0,0,0,0,0,0,0,0,0,0,0,0,0,
  //   0,0,0,0,0,0,0,0,0,0,0,0,0,0,0,0,0,0,0,0,0,0,0,0,0,0,0,0,0,0,0,0,0,0,0,0,0,0,0,0,0,
  //   0,0,0,0,0,0,0,0,0,0,0,0,0,0,0,0,0,0,0,0,0,0,0,0,0,0,0,0,0,0,0,0,0,0,0,0,0,0,0,0,0,
  //   0,0,0,0,0,0,0,0,0,0,0,0,0,0,0,0,0,0,0,0,0,0,0,0,0,0,0,0,0,0,0,0,0,0,0,0,0,0,0,0,0,
  //   0,0,0,0,0,0,0,0,0,0,0,0,0,0,0,0,0,0,0,0,0,0,0,0,0,0,0,0,0,0,0,0,0,0,0,0,9
endmodule
