// Digital circuit RAM.dig as structural Verilog
module RAM (
  input  [15:0] A,
  input  in_2,
  input  Er,
  input  clk,
  output D
);

  wire driver_1_out;
  wire [1:0] d_ff_1_q;

  assign driver_1_out = Er ? A[0] : 1'bz;  // Driver driver_1
  D_FF d_ff_1 (.D(driver_1_out), .C(clk), .Q(d_ff_1_q[0]));  // open: nQ
  RAMSinglePortSel ramsingleportsel_1 (.A(d_ff_1_q), .CS(1'b1), .WE(in_2), .OE(~in_2), .D(D));
  // Pins of 1 and 2 bits meet at d_ff_1_q
  // Pins of 1 and 16 bits meet at A

  // Notes on the sheet:
  //   D: Output going to the MDR
endmodule
