// Digital circuit RRCounter.dig as structural Verilog
module RRCounter (
  input  CLK,
  input  [15:0] SA,
  input  Write,
  input  [15:0] EA,
  output [15:0] A_ROM,
  output nEoa
);

  wire comparator_1_eq;

  CounterPreset #(.Bits(16)) counterpreset_1 (
    .en(nEoa), .C(CLK), .dir(1'b0), .in(SA), .ld(Write), .clr(1'b0), .out(A_ROM));  // open: ovf
  Comparator #(.Bits(16)) comparator_1 (.a(EA), .b(A_ROM), .eq(comparator_1_eq));  // open: gt, lt
  not not_1 (nEoa, comparator_1_eq);
  // Probe on A_ROM

  // Other names for the same wires on the sheet: Eoa = nEoa

  // Notes on the sheet:
  //   A_ROM: address in the ROM
  //   SA: Starting Address
  //   Write: Ending Address
  //   EA: Starting Address
endmodule
