// Digital circuit SAP 2 Architecture.dig as structural Verilog
module SAP_2_Architecture (
  input  [15:0] StartingAddress,
  input  [15:0] EndingAddress,
  input  clk,
  input  Serial_In,
  input  nCLK,
  output [7:0] Q,
  output [35:0] CON,
  output [7:0] IR_Value,
  output [7:0] Accumulator_Value,
  output [15:0] MAR_Output,
  output Sign_Flag,
  output Zero_Flag,
  output [15:0] PC_Ain,
  output [15:0] PC_Counter_Output,
  output [3:0] Sel_Value
);

  wire A_M, ACK, CLK_t, CLR, Ein1, Ein2, keyboard_1_av, Mode, nCLK_t, nCLR, nLo3, nLo4, RESET, So, Step, T1,
       T3, tcounter_18_1_count, treset_1_tclr;
  wire [3:0] output_port_3_1_q, output_port_3_1_q_2;
  wire [7:0] alu_1_flag, iocon_1_iop, KeyOut, mdr_1_oram, pc_1_q, ram_and_rom_1_omdr, tmp_1_tout;
  wire [15:0] keyboard_1_d, pc_1_d;

  Button u_STEP (.out(Step));
  Button u_RESET (.out(RESET));
  TReset treset_1 (
    .CLR(CLR), .TReset(CON[35]), .JumpS(CON[20]), .JumpZ(CON[21]), .JumpNZ(CON[22]), .Zero(Zero_Flag),
    .Sign(Sign_Flag), .TClr(treset_1_tclr));
  DipSwitch #(.dipDefault("true")) Automatic_Manual (.out(A_M));
  ClockGen clockgen_1 (
    .Cin(clk), .RESET(RESET), .nReady(Mode), .St(Step), .nA_M(A_M), .HLT(CON[34]), .nCLR(nCLR), .CLR(CLR),
    .nCLK(nCLK_t), .CLK(CLK_t));
  // Probe on CON[11:8]
  TCounter_18 tcounter_18_1 (.CLK(CLK_t), .CLR(treset_1_tclr), .Count(tcounter_18_1_count), .T1(T1), .T3(T3));
  // Probe on treset_1_tclr
  // Probe on tcounter_18_1_count
  // Probe on {CON[32], CON[25:24]}
  Keyboard keyboard_1 (.C(CLK_t), .en(1'b1), .D(keyboard_1_d), .av(keyboard_1_av));
  // Probe on CON[23]
  RAM_AND_ROM ram_and_rom_1 (
    .IMDR(mdr_1_oram), .OMDR(ram_and_rom_1_omdr), .IMAR(MAR_Output), .EA(EndingAddress), .nCLK(nCLK),
    .SA(StartingAddress), .Write(CLR), .nRun_Prog(Mode), .DIR(CON[17]), .nEoa(Mode));
  // Probe on keyboard_1_d[7:0]
  PC pc_1 (
    .Ep(CON[31]), .Cp(CON[29]), .LAIn(CON[27]), .As(CON[30]), .Ld(CON[28]), .nCLR(nCLR), .nCLK(nCLK_t),
    .PCSel(CON[23]), .Alb(pc_1_q), .Ahb(pc_1_q), .Q(pc_1_q), .Ain(PC_Ain), .DP(PC_Counter_Output), .D(pc_1_d));
  MAR mar_1 (.Q(MAR_Output), .nLm(CON[19]), .CLK(CLK_t), .CLR(CLR), .Msel({CON[32], CON[25:24]}), .A(pc_1_d));
  // Probe on mdr_1_oram
  MDR mdr_1 (
    .DBs(pc_1_q), .OBs(pc_1_q), .ORAM(mdr_1_oram), .IRAM(ram_and_rom_1_omdr), .nLmdr(CON[16]), .DIR(CON[17]),
    .CLK(CLK_t), .Emdr(CON[15]));
  RAMAsync #(.AddrBits(8), .Bits(8)) ramasync_1 (.A({8{1'b0}}), .D(keyboard_1_d[7:0]), .we(keyboard_1_av), .Q(KeyOut));
  Input_port_1 input_port_1_1 (.Q(pc_1_q), .Ein1(Ein1), .Kb(KeyOut), .CLK(CLK_t));
  Input_port_2 input_port_2_1 (.Q(pc_1_q), .Ein2(Ein2), .R(keyboard_1_av), .Si(So), .SinEx(Serial_In), .CLK(CLK_t));
  IR ir_1 (.B(pc_1_q), .C(IR_Value), .nLi(CON[18]), .CLK(CLK_t), .CLR(CLR));
  Sequencer sequencer_1 (.nCLK(nCLK_t), .T3(T3), .T1(T1), .CLR(CLR), .I(IR_Value), .CON(CON));
  // Probe on KeyOut
  // Probe on ram_and_rom_1_omdr
  // Probe on pc_1_q
  ALU alu_1 (.A(Accumulator_Value), .TMP(tmp_1_tout), .Q(pc_1_q), .Sel(CON[11:8]), .El(CON[12]), .Flag(alu_1_flag));
  // Probe on pc_1_q
  B_register b_register_1 (.CLK(CLK_t), .nLb(CON[5]), .Eb(CON[4]), .B(pc_1_q), .Q(pc_1_q));
  // Probe on pc_1_q
  // Probe on pc_1_q
  C_register c_register_1 (.CLK(CLK_t), .nLc(CON[3]), .Ec(CON[2]), .C(pc_1_q), .Q(pc_1_q));
  // Probe on pc_1_q
  // Probe on pc_1_q
  Output_Port_3 output_port_3_1 (.DBs(pc_1_q), .nLo3(nLo3), .Q({output_port_3_1_q_2, output_port_3_1_q}), .CLK(CLK_t));
  Output_Port_4 output_port_4_1 (.DBs(pc_1_q), .nLo4(nLo4), .Q(Q), .So(So), .ACK(ACK), .CLK(CLK_t), .CLR(CLR));
  IOCon iocon_1 (
    .IOp(iocon_1_iop), .nLio(CON[1]), .nCLK(nCLK_t), .CLR(CLR), .Ei1(Ein1), .Ei2(Ein2), .nLo3(nLo3),
    .nLo4(nLo4), .IOEn(CON[0]), .IOSel(pc_1_q));
  Accumulator accumulator_1 (
    .A(pc_1_q), .D(pc_1_q), .CLK(CLK_t), .nLa(CON[14]), .Ea(CON[13]), .ASout(Accumulator_Value));
  TMP tmp_1 (.T(pc_1_q), .D(pc_1_q), .CLK(CLK_t), .nLt(CON[7]), .Et(CON[6]), .Tout(tmp_1_tout));
  // Probe on iocon_1_iop
  // Probe on tmp_1_tout
  Flags flags_1 (.F(alu_1_flag), .Zero(Zero_Flag), .Sign(Sign_Flag), .CLR(CLR), .CLK(CLK_t), .Eflag(CON[26]));
  Seven_Seg_Hex seven_seg_hex_1 (.d(output_port_3_1_q_2), .dp(1'b0));
  Seven_Seg_Hex seven_seg_hex_2 (.d(output_port_3_1_q), .dp(1'b0));

  assign Sel_Value = CON[11:8];

  // Other names for the same wires on the sheet: AccumVal[7:0] = Accumulator_Value; Ain[15:0] = PC_Ain; IOEn = CON[0];
  //   nLio = CON[1]; Ec = CON[2]; nLc = CON[3]; Eb = CON[4]; nLb = CON[5]; Et = CON[6]; nLt = CON[7];
  //   Sel[3:0] = CON[11:8]; Sel_0 = CON[8]; Sel_1 = CON[9]; Sel_2 = CON[10]; Sel_3 = CON[11]; El = CON[12];
  //   Ea = CON[13]; nLa = CON[14]; Emdr = CON[15]; nLmdr = CON[16]; DIR = CON[17]; nLi = CON[18]; nLm = CON[19];
  //   JumpS = CON[20]; JumpZ = CON[21]; JumpNZ = CON[22]; PCSel = CON[23]; Msel[2:0] = {CON[32], CON[25:24]};
  //   Msel_0 = CON[24]; Msel_1 = CON[25]; Eflag = CON[26]; LAIn = CON[27]; Ld = CON[28]; Cp = CON[29]; As = CON[30];
  //   Ep = CON[31]; Msel_2 = CON[32]; HLT = CON[34]; TReset = CON[35]; DP[15:0] = PC_Counter_Output;
  //   IRVal[7:0] = IR_Value; MAROut[15:0] = MAR_Output; nEoa = Mode; Sign = Sign_Flag; We = CLR; Zero = Zero_Flag

  // Notes on the sheet:
  //   EndingAddress: default 4095
  //   clk: Hz: 10
  //   nCLK: Hz: 50000
  //   Dashboard
  //   MAR Controls
  //   Programming Mode Controls:
  //   Controls
endmodule
