// Digital circuit Sequencer.dig as structural Verilog
module Sequencer (
  input  nCLK,
  input  T3,
  input  T1,
  input  CLR,
  input  [7:0] I,
  output [35:0] CON
);

  wire not_1_out, not_2_out, or_1_out;
  wire [7:0] AddressROM_d, counter8wasyncclear_1_q;

  not not_1 (not_1_out, T3);
  or or_1 (or_1_out, T1, CLR);
  ROM #(.AddrBits(8), .Bits(8)) AddressROM (.A(I), .sel(1'b1), .D(AddressROM_d));
  // Probe on AddressROM_d
  not not_2 (not_2_out, or_1_out);
  Counter8wAsyncClear counter8wasyncclear_1 (
    .nLD(not_1_out), .nCLR(not_2_out), .CLK(nCLK), .ENT(1'b1), .ENP(1'b1), .D(AddressROM_d),
    .Q(counter8wasyncclear_1_q));  // open: RCO
  ROM #(.AddrBits(8), .Bits(36)) ControlROM (.A(counter8wasyncclear_1_q), .sel(1'b1), .D(CON));

  // Notes on the sheet:
  //   contents of AddressROM (hex, n*v repeats v):
  //   3,0,0,0,42,48,3a,0,0,0,0,0,44,4a,3d,0,0,0,0,0,0,0,0,68,0,0,0,0,0,0,0,69,0,0,0,0,0,
  //   0,0,0,0,0,0,0,0,0,0,67,0,0,8a,0,0,0,0,0,0,0,76,0,40,46,37,0,0,63,0,0,0,0,0,62,65,
  //   0,0,0,0,0,0,64,0,0,0,0,0,0,0,0,0,0,0,0,0,0,0,0,0,0,0,0,0,0,0,0,0,0,0,0,0,0,0,0,0,
  //   0,0,0,0,0,66,0,60,61,0,0,0,0,0,0,4c,4e,0,0,0,0,0,0,0,0,0,0,0,0,0,0,50,52,0,0,0,0,
  //   0,0,0,0,0,0,0,0,0,0,54,56,0,0,0,0,0,0,58,5a,0,0,0,0,0,0,5c,5e,0,0,0,0,0,0,0,0,0,0,
  //   0,0,0,0,0,0,15,5,0,0,0,0,0,30,c,0,0,27,0,0,0,0,0,a3,0,0,0,0,0,0,0,9e,0,0,0,0,0,0,
  //   0,0,0,0,6a,0,0,0,0,0,0,0,72,0,0,0,0,0,0,0,6e,0,0,0,1e
  //   contents of ControlROM (hex, n*v repeats v):
  //   800540aa,200d40aa,9c0aa,d40aa,8000d40aa,800540aa,80dc0aa,200d40aa,800540aa,480dc0aa,
  //   100d40aa,8000d40aa,800540aa,80dc0aa,200d40aa,800540aa,480dc0aa,200d40aa,2d40aa,100d40aa,
  //   8000d40aa,800540aa,80dc0aa,200d40aa,800540aa,480dc0aa,200d40aa,4d40aa,100d40aa,8000d40aa,
  //   800540aa,80dc0aa,200d40aa,800540aa,480dc0aa,200d40aa,1d40aa,100d40aa,8000d40aa,800540aa,
  //   200d40aa,80dc0aa,810640aa,800540aa,480dc0aa,828640aa,100d40aa,8000d40aa,10540aa,80dc0aa,
  //   20540aa,480dc0aa,100d40aa,200d40aa,8000d40aa,800540aa,200d40aa,8000d80aa,800540aa,
  //   200d40aa,8000dc08a,800540aa,200d40aa,8000dc0a2,d602a,8040d12aa,d403a,8040d5282,d402e,
  //   8040d52a2,d602a,8040d13aa,d403a,8040d538a,d402e,8040d53a2,d403a,8000d10aa,d402e,8000d10aa,
  //   d403a,8000d11aa,d402e,8000d11aa,d403a,8000d14aa,d402e,8000d14aa,d403a,8000d16aa,d402e,
  //   8000d16aa,d403a,8000d15aa,d402e,8000d15aa,8000d608a,8000d60a2,8000d00ba,8000d40b2,
  //   8000d00ae,8000d408e,4000d40aa,8000d18aa,8000d19aa,8000d1aaa,800540aa,200d40aa,dc02a,
  //   8000d142a,800540aa,200d40aa,dc02a,8000d152a,800540aa,200d40aa,dc02a,8000d162a,800540aa,
  //   200d40aa,80dc0aa,830640aa,800540aa,480dc0aa,1808640aa,100d40aa,800540aa,dc0aa,d00aa,
  //   d80aa,d80aa,30540aa,80dc0aa,1000540aa,480dc0aa,100d40aa,200d40aa,8000d40aa,800540aa,
  //   200d40aa,80dc0aa,830640aa,800540aa,480dc0aa,1808640aa,100d40aa,800540aa,e40aa,d60aa,
  //   e60aa,e60aa,30540aa,80dc0aa,1000540aa,480dc0aa,100d40aa,200d40aa,8000d40aa,800540aa,
  //   dc0a8,d00ab,200d40aa,8000d40aa,800540aa,dc0a8,d60ab,200d40aa,8000d40aa
endmodule
