// Digital circuit TCounter.dig as structural Verilog
module TCounter (
  input  CLK,
  input  CLR,
  output T1,
  output T2,
  output T3,
  output T4,
  output T5,
  output T6,
  output T7,
  output T8,
  output T9,
  output T10,
  output T11,
  output T12,
  output T13,
  output T14,
  output T15,
  output T16,
  output T17,
  output T18
);

  D_FF_AS d_ff_as_1 (.Set(CLR), .D(T18), .C(CLK), .Clr(1'b0), .Q(T1));  // open: nQ
  D_FF_AS d_ff_as_2 (.Set(1'b0), .D(T1), .C(CLK), .Clr(CLR), .Q(T2));  // open: nQ
  D_FF_AS d_ff_as_3 (.Set(1'b0), .D(T2), .C(CLK), .Clr(CLR), .Q(T3));  // open: nQ
  D_FF_AS d_ff_as_4 (.Set(1'b0), .D(T3), .C(CLK), .Clr(CLR), .Q(T4));  // open: nQ
  D_FF_AS d_ff_as_5 (.Set(1'b0), .D(T4), .C(CLK), .Clr(CLR), .Q(T5));  // open: nQ
  D_FF_AS d_ff_as_6 (.Set(1'b0), .D(T5), .C(CLK), .Clr(CLR), .Q(T6));  // open: nQ
  D_FF_AS d_ff_as_7 (.Set(1'b0), .D(T6), .C(CLK), .Clr(CLR), .Q(T7));  // open: nQ
  D_FF_AS d_ff_as_8 (.Set(1'b0), .D(T7), .C(CLK), .Clr(CLR), .Q(T8));  // open: nQ
  D_FF_AS d_ff_as_9 (.Set(1'b0), .D(T8), .C(CLK), .Clr(CLR), .Q(T9));  // open: nQ
  D_FF_AS d_ff_as_10 (.Set(1'b0), .D(T9), .C(CLK), .Clr(CLR), .Q(T10));  // open: nQ
  D_FF_AS d_ff_as_11 (.Set(1'b0), .D(T10), .C(CLK), .Clr(CLR), .Q(T11));  // open: nQ
  D_FF_AS d_ff_as_12 (.Set(1'b0), .D(T11), .C(CLK), .Clr(CLR), .Q(T12));  // open: nQ
  D_FF_AS d_ff_as_13 (.Set(1'b0), .D(T12), .C(CLK), .Clr(CLR), .Q(T13));  // open: nQ
  D_FF_AS d_ff_as_14 (.Set(1'b0), .D(T13), .C(CLK), .Clr(CLR), .Q(T14));  // open: nQ
  D_FF_AS d_ff_as_15 (.Set(1'b0), .D(T14), .C(CLK), .Clr(CLR), .Q(T15));  // open: nQ
  D_FF_AS d_ff_as_16 (.Set(1'b0), .D(T15), .C(CLK), .Clr(CLR), .Q(T16));  // open: nQ
  D_FF_AS d_ff_as_17 (.Set(1'b0), .D(T16), .C(CLK), .Clr(CLR), .Q(T17));  // open: nQ
  D_FF_AS d_ff_as_18 (.Set(1'b0), .D(T17), .C(CLK), .Clr(CLR), .Q(T18));  // open: nQ
endmodule
