// Digital circuit TCounter_18.dig as structural Verilog
module TCounter_18 (
  input  CLK,
  input  CLR,
  output T1,
  output T3,
  output [4:0] Count
);

  Counter #(.Bits(5)) counter_1 (.en(1'b1), .C(CLK), .clr(CLR), .out(Count));  // open: ovf
  Comparator #(.Bits(5)) comparator_1 (.a(Count), .b(5'b00011), .eq(T3));  // open: gt, lt
  Comparator #(.Bits(5)) comparator_2 (.a(Count), .b({5{1'b0}}), .eq(T1));  // open: gt, lt
  // Pins of 1 and 5 bits meet at Count
endmodule
