// Digital circuit TMP.dig as structural Verilog
module TMP (
  input  [7:0] T,
  input  nLt,
  input  CLK,
  input  Et,
  output [7:0] D,
  output [7:0] Tout
);

  assign D = Et ? Tout : 8'bz;  // Driver driver_1
  D8_wEnableAsyncClear d8_wenableasyncclear_1 (
    .D0(T[0]), .D1(T[1]), .D2(T[2]), .D3(T[3]), .D4(T[4]), .D5(T[5]), .D6(T[6]), .D7(T[7]), .nE(nLt),
    .CLK(CLK), .CLR(1'b0), .Q0(Tout[0]), .Q1(Tout[1]), .Q2(Tout[2]), .Q3(Tout[3]), .Q4(Tout[4]),
    .Q5(Tout[5]), .Q6(Tout[6]), .Q7(Tout[7]));

  // Notes on the sheet:
  //   T: Input coming from the bus
  //   D: Output going to the bus
endmodule
