// Digital circuit TReset.dig as structural Verilog
module TReset (
  input  CLR,
  input  TReset,
  input  JumpS,
  input  JumpZ,
  input  JumpNZ,
  input  Zero,
  input  Sign,
  output TClr
);

  wire and_1_out, and_2_out, and_3_out;

  and and_1 (and_1_out, JumpZ, ~Zero);  // And
  and and_2 (and_2_out, JumpNZ, Zero);
  and and_3 (and_3_out, JumpS, ~Sign);  // And
  or or_1 (TClr, CLR, TReset, and_1_out, and_2_out, and_3_out);
endmodule
